# Fritzing sketch EMPulser (saved by Fritzing 0.9.3b)
circuit board: 6cm x 4cm
breadboards: 1

parts:
  IRF530 = Basic FET N-Channel [package="TO220 [THT]"]
  VCC1 = Battery block 9V
  R1 = Resistor [tolerance=±5% resistance=10k package=THT]
  PN2222A = NPN-Transistor [package="TO92 [THT]"]
  D1 = Rectifier Diode [part_number=1N4007 package="300 mil [THT]"]
  J1 = female pin header, 1 pin [form="♀ (female)"]
  J2 = female pin header, 1 pin [form="♀ (female)"]
  Test = female pin header, 1 pin [form="♀ (female)"]
  GND = female pin header, 1 pin [form="♀ (female)"]
  SS441R = mystery part, 3 pins [chip_label=?]
  R2 = Resistor [tolerance=±5% resistance=10k package=THT]

nets:
  N1: IRF530.gate, PN2222A.C, R2.Pin_0
  N2: IRF530.drain, D1.anode, J1.pin1
  GND: IRF530.source, VCC1.-, PN2222A.E, GND.pin1, SS441R.pin2
  N3: VCC1.+, R1.Pin_0, D1.cathode, J2.pin1, SS441R.pin1, R2.Pin_1
  N4: R1.Pin_1, PN2222A.B, Test.pin1, SS441R.pin3

notes:
  OUT
  GND
  VS
  Inductor
  EM Hall Pulser
  2017 - S.Irons
  Solenoid
  5-10VDC
  Yale University
